// Logisim project nj.circ as structural Verilog: 2 circuits, main circuit full adder
module full_adder (
  input  in_1,
  input  in_2,
  input  in_3,
  output out_4,
  output out_5
);

  wire and_1_out, and_2_out, xor_1_out;

  xor xor_1 (xor_1_out, in_1, in_2);
  and and_1 (and_1_out, in_1, in_2);
  xor xor_2 (out_4, xor_1_out, in_3);
  and and_2 (and_2_out, xor_1_out, in_3);
  or or_1 (out_5, and_2_out, and_1_out);
endmodule

module alu (
  input  in_1,
  input  in_2,
  input  in_3,
  input  in_4,
  input  in_5,
  input  in_6,
  input  in_7,
  input  in_8,
  input  in_9,
  input  in_10,
  input  in_11,
  output out_12,
  output out_13,
  output out_14,
  output out_15,
  output out_16
);

  wire and_1_out, and_2_out, and_3_out, and_4_out, and_5_out, and_6_out, and_7_out, and_8_out,
       full_adder_1_out_5, full_adder_2_out_5, full_adder_3_out_5, not_1_out, not_2_out, not_3_out,
       not_4_out, or_1_out, or_2_out, or_3_out, or_4_out;

  not not_1 (not_1_out, in_11);
  and and_1 (and_1_out, in_5, in_3);
  not not_2 (not_2_out, in_5);
  and and_2 (and_2_out, in_3, in_7);
  not not_3 (not_3_out, in_7);
  and and_3 (and_3_out, in_9, in_3);
  not not_4 (not_4_out, in_9);
  and and_4 (and_4_out, in_11, in_3);
  and and_5 (and_5_out, in_2, not_1_out);
  and and_6 (and_6_out, not_2_out, in_2);
  and and_7 (and_7_out, not_3_out, in_2);
  or or_1 (or_1_out, and_3_out, and_8_out);
  and and_8 (and_8_out, not_4_out, in_2);
  or or_2 (or_2_out, and_4_out, and_5_out);
  or or_3 (or_3_out, and_1_out, and_6_out);
  or or_4 (or_4_out, and_2_out, and_7_out);
  full_adder full_adder_1 (.in_1(in_1), .in_2(in_4), .in_3(or_3_out), .out_4(out_12), .out_5(full_adder_1_out_5));
  full_adder full_adder_2 (
    .in_1(full_adder_1_out_5), .in_2(in_6), .in_3(or_4_out), .out_4(out_13), .out_5(full_adder_2_out_5));
  full_adder full_adder_3 (
    .in_1(full_adder_2_out_5), .in_2(in_8), .in_3(or_1_out), .out_4(out_14), .out_5(full_adder_3_out_5));
  full_adder full_adder_4 (.in_1(full_adder_3_out_5), .in_2(in_10), .in_3(or_2_out), .out_4(out_15), .out_5(out_16));
endmodule
